# Fritzing sketch voltmeter clock (saved by Fritzing 0.9.5d)
circuit board: 10.5396cm x 6.64496cm
breadboards: 1

parts:
  Clock = Itsy Bitsy 32u4 5V @ 16MHz [part_number="Adafruit #3677"]
  LEDs = Itsy Bitsy 32u4 5V @ 16MHz [part_number="Adafruit #3677"]
  Hour_LED = Adafruit Breadboard-Friendly NeoPixel [part_number="Adafruit #1312"]
  Minute_LED = Adafruit Breadboard-Friendly NeoPixel [part_number="Adafruit #1312"]
  Second_LED = Adafruit Breadboard-Friendly NeoPixel [part_number="Adafruit #1312"]
  ZS-042_RTC1 = ZS-042 RTC Module
  J1 = Power Jack [package=power_jack_slot]
  Hour = Voltmeter
  Minute = Voltmeter
  Second = Voltmeter
  S_M = SWITCH-MOMENTARY-2 [package=tactile_switch_tall]
  S_+ = SWITCH-MOMENTARY-2 [package=tactile_switch_tall]
  S_2 = SWITCH-MOMENTARY-2 [package=tactile_switch_tall]
  S_- = SWITCH-MOMENTARY-2 [package=tactile_switch_tall]
  S_H = SWITCH-MOMENTARY-2 [package=tactile_switch_tall]
  S_1 = SWITCH-MOMENTARY-2 [package=tactile_switch_tall]
  R1 = Resistor [tolerance=±5% resistance=470 package=THT]
  C1 = Tantalum Capacitor [capacitance=0.1mF package="D 7343 [SMD, tantalum]"]
  C3 = Tantalum Capacitor [capacitance=0.1mF package="D 7343 [SMD, tantalum]"]
  C2 = Tantalum Capacitor [capacitance=0.1mF package="D 7343 [SMD, tantalum]"]

nets:
  N1: Clock.GND, S_M.1, S_+.1, S_2.1, S_-.1, S_H.1, S_1.1
  12V: Clock.VBAT, LEDs.VBAT, J1.PWR
  N2: Clock.D13, Hour.Positive
  N3: Clock.D12, Minute.Positive
  N4: Clock.D11, Second.Positive
  N5: Clock.D9, LEDs.D9
  N6: Clock.D7, LEDs.D7
  N7: Clock.SCL, ZS-042_RTC1.SCL
  N8: Clock.SDA, ZS-042_RTC1.SDA
  N9: Clock.A5, S_2.2
  N10: Clock.A4, S_1.2
  N11: Clock.A3, S_-.2
  N12: Clock.A2, S_+.2
  N13: Clock.A1, S_M.2
  N14: Clock.A0, S_H.2
  RTC Power: Clock.+5V, ZS-042_RTC1.VCC
  GND: LEDs.GND, Hour_LED.GND, Minute_LED.GND, Second_LED.GND, ZS-042_RTC1.GND, J1.GND, Hour.Com, Minute.Com, Second.Com, C1.-, C3.-, C2.-
  N15: LEDs.A0, R1.Pin_0
  LED Power: LEDs.+5V, Hour_LED.VDD, Minute_LED.VDD, Second_LED.VDD, C1.+, C3.+, C2.+
  N16: Hour_LED.IN, R1.Pin_1
  N17: Hour_LED.OUT, Minute_LED.IN
  N18: Minute_LED.OUT, Second_LED.IN

custom parts:
  Itsy Bitsy 32u4 5V @ 16MHz: What's smaller than a Feather but larger than a Trinket? It's an Itsy Bitsy! Small, powerful, Arduino-compatible - this microcontroller board is perfect when you want something very compact, but still with a bunch of pins. Itsy Bitsy is only 1.4" long by 0.7" wide, but has 6 power pins, 6 analog & digital pins and 17 digital pins. It packs much of the same capability as an Arduino UNO. So it's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
  Adafruit Breadboard-Friendly NeoPixel: This is the easiest way possible to add small, bright RGB pixels to your project. We took the same technology from our Flora NeoPixels and made them breadboard friendly, with two rows of 3 x 0.1" spaced header on each side for easy soldering, chaining and breadboarding. These ultra-bright LEDs have a constant-current driver cooked right into the LED package! The pixels are chainable - so you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
  Voltmeter: A Standard Multimeter in Current mode
